# Fritzing sketch HwWeapons (saved by Fritzing 0.9.3b)
stripboards: 1

parts:
  MCU1 = Raspberry Pi Zero
  IC1 = IC, DIP package, 28 pins [chip_label=IC]
  S1 = Round Pushbutton
  S2 = Round Pushbutton
  S3 = Round Pushbutton
  S4 = Round Pushbutton
  S5 = Round Pushbutton
  S6 = Round Pushbutton
  S7 = Round Pushbutton
  S8 = Round Pushbutton
  S9 = Round Pushbutton
  S10 = Round Pushbutton
  S11 = Round Pushbutton
  S12 = Round Pushbutton
  S13 = Round Pushbutton
  S14 = Round Pushbutton
  S15 = Round Pushbutton
  S16 = Round Pushbutton
  S17 = Round Pushbutton
  S18 = Round Pushbutton
  S19 = Round Pushbutton
  S20 = Taiway 100-SP-X-T1 SPDT Miniature Toggle Switch [part_number=100-SP-X-T1-0-0-B1-M1 package=THT]
  S21 = Taiway 100-SP-X-T1 SPDT Miniature Toggle Switch [part_number=100-SP-X-T1-0-0-B1-M1 package=THT]
  RE1 = Rotary Encoder [package=THT]
  RE2 = Rotary Encoder [package=THT]
  RE3 = Rotary Encoder [package=THT]
  LED2 = LED - 5mm [color="Red (633nm)" package="5 mm [THT]"]  # not connected
  S22 = Taiway 100-SP-X-T1 SPDT Miniature Toggle Switch [part_number=100-SP-X-T1-0-0-B1-M1 package=THT]
  S23 = Round Pushbutton
  ADC1 = MCP3008 [package=dil16]
  U1 = POT [package=pot_alpha_rv16af-20]

nets:
  N1: MCU1.pin_1, MCU1.pin_6, MCU1.pin_9, MCU1.pin_14, MCU1.pin_17, MCU1.pin_20, MCU1.pin_25, MCU1.pin_30, MCU1.pin_34, MCU1.pin_39, IC1.pin9, IC1.pin10, IC1.pin15, IC1.pin16, IC1.pin17, IC1.pin18, S1.leg0, S2.leg0, S3.leg0, S4.leg0, S5.leg0, S6.leg0, S7.leg0, S8.leg1, S9.leg1, S10.leg1, S11.leg1, S12.leg1, S13.leg1, S14.leg1, S15.leg0, S16.leg0, S17.leg0, S18.leg0, S19.leg0, S20.L1, S20.L2, S21.L1, S21.L2, RE2.EncoderPinB, RE3.EncoderPinB, S22.L1, S22.L2, S23.leg0, ADC1.AGND, ADC1.VREF, ADC1.VDD, U1.A, U1.E
  N2: MCU1.pin_2, MCU1.pin_4, RE1.EncoderPinB
  N3: MCU1.pin_3, IC1.pin13
  N4: MCU1.pin_5, IC1.pin12
  N5: MCU1.pin_7, S21.COM
  N6: MCU1.pin_8, S16.leg1
  N7: MCU1.pin_10, S17.leg1
  N8: MCU1.pin_11, S22.COM
  N9: MCU1.pin_13, S23.leg1
  N10: MCU1.pin_16, S18.leg1
  N11: MCU1.pin_18, RE1.EncoderPinA
  N12: MCU1.pin_19, ADC1.Din
  N13: MCU1.pin_21, ADC1.Dout
  N14: MCU1.pin_22, RE1.EncoderPinC
  N15: MCU1.pin_23, ADC1.CLK
  N16: MCU1.pin_24, ADC1.CS/SHDN
  N17: MCU1.pin_26, S19.leg1
  N18: MCU1.pin_27, IC1.pin20
  N19: MCU1.pin_32, RE2.EncoderPinA
  N20: MCU1.pin_36, RE2.EncoderPinC
  N21: MCU1.pin_38, RE3.EncoderPinA
  N22: MCU1.pin_40, RE3.EncoderPinC
  N23: IC1.pin1, S11.leg0
  N24: IC1.pin2, S14.leg0
  N25: IC1.pin3, S13.leg0
  N26: IC1.pin4, S9.leg0
  N27: IC1.pin5, S12.leg0
  N28: IC1.pin6, S10.leg0
  N29: IC1.pin7, S8.leg0
  N30: IC1.pin8, S20.COM
  N31: IC1.pin21, S15.leg1
  N32: IC1.pin22, S7.leg1
  N33: IC1.pin23, S6.leg1
  N34: IC1.pin24, S5.leg1
  N35: IC1.pin25, S4.leg1
  N36: IC1.pin26, S3.leg1
  N37: IC1.pin27, S2.leg1
  N38: IC1.pin28, S1.leg1
  N39: ADC1.CH0, U1.S

notes:
  Laukaise putki
  Valitse ase
  Lataa putki
  Target
  Shield
  Beam
  Self destruct
  Calibrate
  LED lähtö
  Beam target
  (optinen)
  5 V
